# Fritzing sketch 1_pcb_esc_2_port (saved by Fritzing 0.9.3b)
circuit board: 5.54895cm x 15cm
breadboards: 1

parts:
  JP5 = Header 3 [package=jst-3-pth]
  JP6 = Header 3 [package=jst-3-pth]
  JP2 = Header 3 [package=jst-3-smd]

nets:
  N1: JP5.2, JP2.2
  N2: JP5.3, JP6.3, JP2.1
  N3: JP6.1, JP2.3

notes:
  +
  -
