# Fritzing sketch 2_pcb_esc_2_horizontal_20x10 (saved by Fritzing 0.9.3b)
circuit board: 20cm x 8cm
breadboards: 1

parts:
  J1 = female pin header, 3 pins [form="♀ (female)"]
  J3 = female pin header, 3 pins [form="♀ (female)"]
  JP1 = Header 1 [package=smtso-256-et]
  JP2 = Header 1 [package=smtso-256-et]
  JP3 = Header 1 [package=smtso-256-et]
  JP4 = Header 1 [package=smtso-256-et]
  JP5 = Header 1 [package=smtso-256-et]
  JP6 = Header 1 [package=smtso-256-et]
  J2 = female alternating pin header, 3 pins [form="♀ (female)"]
  JP7 = Header 1 [package=smtso-256-et]
  JP8 = Header 1 [package=smtso-256-et]
  JP9 = Header 1 [package=smtso-256-et]
  JP10 = Header 1 [package=smtso-256-et]
  JP12 = Header 1 [package=smtso-256-et]
  JP11 = Header 1 [package=smtso-256-et]
  JP13 = Header 1 [package=smtso-256-et]
  JP14 = Header 1 [package=smtso-256-et]
  JP15 = Header 1 [package=smtso-256-et]
  JP16 = Header 1 [package=smtso-256-et]
  JP17 = Header 1 [package=smtso-256-et]

nets:
  N1: J1.pin1, J1.pin2, J3.pin2, J3.pin3, J2.pin3
  N2: J1.pin3, J2.pin1
  N3: JP1.1, JP2.1
  N4: JP3.1, JP4.1
  N5: JP5.1, JP6.1
  N6: JP7.1, JP8.1
  N7: JP9.1, JP10.1
  N8: JP12.1, JP11.1
  N9: JP13.1, JP16.1
  N10: JP14.1, JP15.1, JP17.1

notes:
  -
  +
